# Fritzing sketch core_schema (saved by Fritzing 0.9.5d)
breadboards: 1

parts:
  Espessif_Serial_Wifi_Modul_1 = ESP8266 ESP01 [part_number=ESP8266 package=THT]
  부품5 = FC-28 Soil Hygrometer Module - Probe
  부품6 = FC-28 Soil Hygrometer Module
  WeMos_D1_Mini_Relay_Shield_V1 = WeMos D1 Mini Relay Shield V2
  Part4 = Arduino Nano (Rev3.0)
  R1 = Resistor [tolerance=±5% resistance=220 package=THT]
  VCC1 = Battery  # not connected
  WATER_PUMP2 = water pump/motor  # not connected

nets:
  GND: Espessif_Serial_Wifi_Modul_1.GND, 부품6.GND, WeMos_D1_Mini_Relay_Shield_V1.G, Part4.GND
  N1: Espessif_Serial_Wifi_Modul_1.RXD, R1.Pin_0
  N2: Espessif_Serial_Wifi_Modul_1.TXD, Part4.D2
  VCC: Espessif_Serial_Wifi_Modul_1.VCC, Espessif_Serial_Wifi_Modul_1.CH_PD, Part4.3V3
  N3: 부품5.POS, 부품6.POS
  N4: 부품5.NEG, 부품6.NEG
  N5: 부품6.VCC, Part4.D7
  N6: 부품6.AO, Part4.A0
  5V: WeMos_D1_Mini_Relay_Shield_V1.5V, Part4.5V
  N7: WeMos_D1_Mini_Relay_Shield_V1.D4, Part4.D4
  N8: Part4.D3, R1.Pin_1

notes:
  TX GND
  EN IG2
  RST IG1
  3v3 RX

custom parts:
  ESP8266 ESP01: Generic WiFi Module based on the ESP8266 with onboard PCB antenna and UART communications
  FC-28 Soil Hygrometer Module - Probe: The FC-28 is a soil hygrometer module that uses the Texas Instruments LM393 comparator chip to provide an analog measurement of soil humidity.
  FC-28 Soil Hygrometer Module: The FC-28 is a soil hygrometer module that uses the Texas Instruments LM393 comparator chip to provide an analog measurement of soil humidity. The digital output is high when soil moisture is over a certain threshold, as determined by adjusting the potentiometer.
  water pump/motor: WATER PUMP BY ARDUBLOCKTR
