# Fritzing sketch moisture_sensor_schema (saved by Fritzing 0.9.5d)

parts:
  부품3 = FC-28 Soil Hygrometer Module - Probe
  부품4 = FC-28 Soil Hygrometer Module
  Part1 = Arduino Nano (Rev3.0)

nets:
  N1: 부품3.POS, 부품4.POS
  N2: 부품3.NEG, 부품4.NEG
  N3: 부품4.VCC, Part1.D7
  GND: 부품4.GND, Part1.GND
  N4: 부품4.AO, Part1.A0

custom parts:
  FC-28 Soil Hygrometer Module - Probe: The FC-28 is a soil hygrometer module that uses the Texas Instruments LM393 comparator chip to provide an analog measurement of soil humidity.
  FC-28 Soil Hygrometer Module: The FC-28 is a soil hygrometer module that uses the Texas Instruments LM393 comparator chip to provide an analog measurement of soil humidity. The digital output is high when soil moisture is over a certain threshold, as determined by adjusting the potentiometer.
