# Fritzing sketch voltae_sensor_schema (saved by Fritzing 0.9.5d)

parts:
  Part1 = Arduino Nano (Rev3.0)
  Part2 = Voltage Sensor 25V
  U1 = LIPO-110mAh [package=lipo-110]

nets:
  N1: Part1.GND, Part2.-
  N2: Part1.A0, Part2.S
  N3: Part2.GND, U1.-
  N4: Part2.VCC, Part2.+, U1.+
