# Fritzing sketch wifi-module (saved by Fritzing 0.9.5d)
breadboards: 1

parts:
  Part1 = Arduino Nano (Rev3.0) (ICSP)
  Espessif_Serial_Wifi_Modul_1 = ESP8266 ESP01 [part_number=ESP8266 package=THT]
  R2 = Resistor [tolerance=±5% resistance=220 package=THT]
  R3 = Resistor [tolerance=±5% resistance=220 package=THT]
  LED1 = LED - 5mm [color="Red (633nm)" package="5 mm [THT]"]

nets:
  N1: Part1.D2, Espessif_Serial_Wifi_Modul_1.TXD
  N2: Part1.D3, R2.Pin_0
  N3: Part1.D9, R3.Pin_1
  VIN: Part1.VIN, Espessif_Serial_Wifi_Modul_1.GND, LED1.cathode
  3V3: Part1.3V3, Espessif_Serial_Wifi_Modul_1.VCC, Espessif_Serial_Wifi_Modul_1.CH_PD
  N4: Espessif_Serial_Wifi_Modul_1.RXD, R2.Pin_1
  N5: R3.Pin_0, LED1.anode

notes:
  TX GND
  EN IG2
  RST IG1
  3v3 RX

custom parts:
  ESP8266 ESP01: Generic WiFi Module based on the ESP8266 with onboard PCB antenna and UART communications
